# Fritzing sketch c3 (saved by Fritzing 1.0.1rc)

parts:
  A1 = Esp32-c3 super mini
  Part1 = BH1750
  YL-83_-_Detection_Board1 = YL-83 Rain Sensor - Detection Board  # not connected
  DHT1 = DHT11 Humitidy and Temperature Sensor (3 pins)
  Part2 = Adafruit ADS1115 16Bit I2C ADC [part_number="Adafruit #1085"]  # not connected

nets:
  N1: A1.Pin_4, Part1.SDA
  N2: A1.Pin_5, Part1.SCL
  N3: A1.Pin_6, DHT1.Signal
  N4: A1.Pin_14, DHT1.Plus
  GND: A1.Pin_15, Part1.GND, DHT1.Gnd
  N5: A1.Pin_16, Part1.VCC

custom parts:
  Esp32-c3 super mini: ESP32-C3 Development Board ESP32 SuperMini Development Board ESP32 Development Board WiFi Bluetooth.
  BH1750: Light Sensor
  YL-83 Rain Sensor - Detection Board: The YL-83 is a rain sensor that has more resistance when dry and less resistance when wet. The module runs at 5V.
  DHT11 Humitidy and Temperature Sensor (3 pins): DHT11 Humidity and Temperature Sensor (3 pins).
  Adafruit ADS1115 16Bit I2C ADC: For microcontrollers without an analog-to-digital converter or when you want a higher-precision ADC, the ADS1115 provides 16-bit precision at 860 samples/second over I2C. The chip can be configured as 4 single-ended input channels, or two differential channels. As a nice bonus, it even includes a programmable gain amplifier, up to x16, to help boost up smaller single/differential signals to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
